# Fritzing sketch sherman (saved by Fritzing 0.9.3b)
breadboards: 1

parts:
  Componente4 = Arduino XBee Shield
  Componente5 = Bluetooth Module Breakout - Roving Networks (RN-41)
  U1 = L298 [package=multiwatt15]  # not connected
  U2 = L298 [package=multiwatt15]  # not connected
  M1 = DC Motor  # not connected
  M2 = DC Motor  # not connected

nets:
  N1: Componente4.N$31, Componente5.GND
  N2: Componente4.N$32, Componente5.RESET
  N3: Componente4.N$33, Componente5.SPICLK
  N4: Componente4.N$34, Componente5.PIO7
  N5: Componente4.N$35, Componente5.PIO6
  N6: Componente4.N$36, Componente5.SPIMOSI
  N7: Componente4.N$37, Componente5.PIO10
  N8: Componente4.N$39, Componente5.PIO11
  N9: Componente4.N$40, Componente5.10
  N10: Componente4.N$128, Componente5.UARTTX
  N11: Componente4.N$129, Componente5.UARTRTS
  N12: Componente4.N$130, Componente5.UARTCTS
  N13: Componente4.N$131, Componente5.PIO2
  N14: Componente4.N$132, Componente5.PIO3
  N15: Componente4.N$133, Componente5.PIO5
  N16: Componente4.N$134, Componente5.PIO4
  N17: Componente4.N$135, Componente5.SPICSB
  N18: Componente4.N$136, Componente5.SPIMISO
